# Fritzing sketch conexionado (saved by Fritzing 0.9.3b)
breadboards: 1

parts:
  MCU1 = STM32 Blue Pill [part_number=STM32F103C8T6]
  Motor_paso_a_paso = 28BYJ-48 Stepper Motor [part_number=28BYJ-48]
  Driver = 28BYJ-48 Driver Module [part_number=ULN2003 package=THT]
  Sensor_de_temperatura = LM35 Temperature Sensor [package="TO92 [THT]"]
  Fin_de_carrera_izquierdo = Momentary Switch [package=ksa_sealed_tac_switch]
  Motor = smd LED [color="Green (565nm)" package="0603 [SMD]"]
  R1 = Resistor [tolerance=±5% resistance=220 package=THT]
  R2 = Resistor [tolerance=±5% resistance=220 package=THT]
  Cooler = smd LED [color="Blue (470nm)" package="0603 [SMD]"]
  Fin_de_carreara_derecho = Momentary Switch [package=ksa_sealed_tac_switch]
  Sw_manual = Momentary Switch [package=ksa_sealed_tac_switch]
  J1 = Piezo Speaker [part_number="Buzzer pasivo"]
  Conversor_USB_SERIE = USB-TTL UART

nets:
  N1: MCU1.pin5, Sw_manual.4
  N2: MCU1.pin6, Conversor_USB_SERIE.pin9
  N3: MCU1.pin7, Conversor_USB_SERIE.pin8
  N4: MCU1.pin10, Driver.GND, Fin_de_carrera_izquierdo.1, Motor.anode, Cooler.anode, Fin_de_carreara_derecho.1, Sw_manual.2, J1.pin1, Conversor_USB_SERIE.pin6
  N5: MCU1.pin17, J1.pin2
  N6: MCU1.pin18, Driver.Vmotor
  N7: MCU1.pin19, MCU1.pin_39, MCU1.pin_40
  N8: MCU1.pin20, MCU1.pin38, Sensor_de_temperatura.+Vs
  N9: MCU1.pin25, Sensor_de_temperatura.Vout
  N10: MCU1.pin26, Driver.IN4
  N11: MCU1.pin27, Driver.IN3
  N12: MCU1.pin28, Driver.IN2
  N13: MCU1.pin29, Driver.IN1
  N14: MCU1.pin30, Fin_de_carrera_izquierdo.3
  N15: MCU1.pin31, Fin_de_carreara_derecho.3
  N16: MCU1.pin32, R1.Pin_1
  N17: MCU1.pin33, R2.Pin_1
  N18: Motor_paso_a_paso.blue-pin, Driver.blue-pin
  N19: Motor_paso_a_paso.pink-pin, Driver.pink-pin
  N20: Motor_paso_a_paso.yellow-pin, Driver.yellow-pin
  N21: Motor_paso_a_paso.orange-pin, Driver.orange-pin
  N22: Motor_paso_a_paso.red-pin, Driver.red-pin
  N23: Motor.cathode, R1.Pin_0
  N24: R2.Pin_0, Cooler.cathode

custom parts:
  STM32 Blue Pill: The STM32 family of 32-bit microcontrollers based on the Arm Cortex-M processor is designed to offer new degrees of freedom to MCU users. It offers products combining very high performance, real-time capabilities, digital signal processing, low-power / low-voltage operation, and connectivity, while maintaining full integration and ease of development.
  28BYJ-48 Stepper Motor: Unipolar Stepper Motor 28BYJ-48 Top coil - pink & orange Bottom coil - blue & yellow Common rail - red Connector pins: blue - pink - yellow - orange - red
  28BYJ-48 Driver Module: Generic male header
  USB-TTL UART: USB programmer interface incorporating Silicon Labs CP2102 UART
